// Logisim project ALU.circ as structural Verilog: 5 circuits, main circuit main
module main (
  input  [7:0] in_1
);

  wire [7:0] PC_q;

  PC PC (.Q(PC_q));
  Instruction_Memory Instruction_Memory (.A(PC_q), .D(in_1));
endmodule

module ALU (
  input  [31:0] A,
  input  [31:0] B,
  input  [3:0] ALUFN,
  output [31:0] OUT
);

  wire and_2_out, comparator_1_eq, comparator_1_lt;
  wire [31:0] adder_1_out, and_1_out, bit_extender_1_out, bit_extender_2_out, bit_extender_3_out,
       divider_1_out, multiplier_1_out, or_1_out, shifter_1_out, shifter_2_out, shifter_3_out,
       subtractor_1_out, xor_1_out;

  Divider #(.width(32)) divider_1 (.a(A), .b(B), .out(divider_1_out));  // open: upper, rem
  Multiplier #(.width(32)) multiplier_1 (.a(A), .b(B), .out(multiplier_1_out));  // open: cin, cout
  Subtractor #(.width(32)) subtractor_1 (.a(A), .b(B), .out(subtractor_1_out));  // open: bin, bout
  Adder #(.width(32)) adder_1 (.a(A), .b(B), .out(adder_1_out));  // open: cin, cout
  assign and_1_out = A & B;  // AND_Gate and_1, 32 bits wide
  assign or_1_out = A | B;  // OR_Gate or_1, 32 bits wide
  Multiplexer #(.select(4), .width(32)) multiplexer_1 (
    .in1(adder_1_out), .in2(subtractor_1_out), .in3(multiplier_1_out), .in4(divider_1_out), .in5(and_1_out),
    .in6(or_1_out), .in7(xor_1_out), .in8(bit_extender_2_out), .in9(bit_extender_3_out),
    .in10(bit_extender_1_out), .in11(shifter_3_out), .in12(shifter_2_out), .in13(shifter_1_out), .out(OUT),
    .sel(ALUFN));  // open: in0, in14, in15, en
  assign xor_1_out = A ^ B;  // XOR_Gate xor_1, 32 bits wide
  Comparator #(.width(32)) comparator_1 (.a(A), .b(B), .eq(comparator_1_eq), .lt(comparator_1_lt));  // open: gt
  assign bit_extender_1_out = {{31{1'b0}}, comparator_1_eq};  // Bit_Extender bit_extender_1
  and and_2 (and_2_out, comparator_1_eq, comparator_1_lt);
  assign bit_extender_2_out = {{31{1'b0}}, comparator_1_lt};  // Bit_Extender bit_extender_2
  assign bit_extender_3_out = {{31{1'b0}}, and_2_out};  // Bit_Extender bit_extender_3
  Shifter #(.width(32), .shift("ar")) shifter_1 (.in(B), .\dist (A[4:0]), .out(shifter_1_out));
  Shifter #(.width(32), .shift("lr")) shifter_2 (.in(B), .\dist (A[4:0]), .out(shifter_2_out));
  Shifter #(.width(32)) shifter_3 (.in(B), .\dist (A[4:0]), .out(shifter_3_out));
endmodule

module Register_File (
  input  WE,
  input  [4:0] WA,
  input  [31:0] WD,
  input  [4:0] RA1,
  input  [4:0] RA2,
  output [31:0] RD1,
  output [31:0] RD2
);

  wire clock_1_out, demultiplexer_1_out0, demultiplexer_1_out1, demultiplexer_1_out2, demultiplexer_1_out3,
       demultiplexer_1_out4, demultiplexer_1_out29, demultiplexer_1_out30;
  wire [31:0] r0_q, r1_q, r2_q, r3_q, r4_q, r29_q, r30_q;

  Clock clock_1 (.out(clock_1_out));
  Register #(.width(32)) r0 (.D(WD), .en(demultiplexer_1_out0), .Q(r0_q), .clk(clock_1_out));  // open: clr
  Multiplexer #(.select(5), .width(32)) multiplexer_1 (
    .in0(r0_q), .in1(r1_q), .in2(r2_q), .in3(r3_q), .in4(r4_q), .in29(r29_q), .in30(r30_q),
    .in31({32{1'b0}}), .out(RD1), .sel(RA1));  // open: in5, in6, in7, in8, in9, in10, in11, in12, in13, in14, in15, in16, in17, in18, in19, in20, in21, in22, in23, in24, in25, in26, in27, in28, en
  Demultiplexer #(.select(5)) demultiplexer_1 (
    .out0(demultiplexer_1_out0), .out1(demultiplexer_1_out1), .out2(demultiplexer_1_out2),
    .out3(demultiplexer_1_out3), .out4(demultiplexer_1_out4), .out29(demultiplexer_1_out29),
    .out30(demultiplexer_1_out30), .in(WE), .sel(WA));  // open: out5, out6, out7, out8, out9, out10, out11, out12, out13, out14, out15, out16, out17, out18, out19, out20, out21, out22, out23, out24, out25, out26, out27, out28, out31, en
  Register #(.width(32)) r1 (.D(WD), .en(demultiplexer_1_out1), .Q(r1_q), .clk(clock_1_out));  // open: clr
  Register #(.width(32)) r3 (.D(WD), .en(demultiplexer_1_out3), .Q(r3_q), .clk(clock_1_out));  // open: clr
  Register #(.width(32)) r2 (.D(WD), .en(demultiplexer_1_out2), .Q(r2_q), .clk(clock_1_out));  // open: clr
  Register #(.width(32)) r4 (.D(WD), .en(demultiplexer_1_out4), .Q(r4_q), .clk(clock_1_out));  // open: clr
  Multiplexer #(.select(5), .width(32)) multiplexer_2 (
    .in0(r0_q), .in1(r1_q), .in2(r2_q), .in3(r3_q), .in4(r4_q), .in29(r29_q), .in30(r30_q),
    .in31({32{1'b0}}), .out(RD2), .sel(RA2));  // open: in5, in6, in7, in8, in9, in10, in11, in12, in13, in14, in15, in16, in17, in18, in19, in20, in21, in22, in23, in24, in25, in26, in27, in28, en
  Register #(.width(32)) r29 (.D(WD), .en(demultiplexer_1_out29), .Q(r29_q), .clk(clock_1_out));  // open: clr
  Register #(.width(32)) r30 (.D(WD), .en(demultiplexer_1_out30), .Q(r30_q), .clk(clock_1_out));  // open: clr
endmodule

module Instruction_Memory (
  input  [7:0] A,
  output [7:0] D
);

  wire [31:0] rom_1_data;

  ROM #(.dataWidth(32)) rom_1 (.addr(A), .data({rom_1_data[31:10], D, rom_1_data[1:0]}));  // open: sel
endmodule

module PC (
  output [7:0] Q
);

  wire clock_1_out, Reset_out;
  wire [7:0] adder_1_out, multiplexer_1_out;

  Button Reset (.out(Reset_out));
  Multiplexer #(.width(8)) multiplexer_1 (
    .in0(adder_1_out), .in1({8{1'b0}}), .out(multiplexer_1_out), .sel(Reset_out));  // open: en
  Clock clock_1 (.out(clock_1_out));
  Register register_1 (.D(multiplexer_1_out), .Q(Q), .clk(clock_1_out));  // open: en, clr
  Adder adder_1 (.a(Q), .b(8'h4), .out(adder_1_out));  // open: cin, cout
endmodule
