// Logisim project Counter.circ as structural Verilog: 1 circuit, main circuit main
module main (
  output [31:0] Q
);

  wire clock_1_out, Reset_out;
  wire [31:0] adder_1_out, multiplexer_1_out;

  Button Reset (.out(Reset_out));
  Multiplexer #(.width(32)) multiplexer_1 (
    .in0(adder_1_out), .in1({32{1'b0}}), .out(multiplexer_1_out), .sel(Reset_out));  // open: en
  Clock clock_1 (.out(clock_1_out));
  Register #(.width(32)) register_1 (.D(multiplexer_1_out), .Q(Q), .clk(clock_1_out));  // open: en, clr
  Adder #(.width(32)) adder_1 (.a(Q), .b(32'h4), .out(adder_1_out));  // open: cin, cout
endmodule
